// Logisim project logisim-obvod 60.circ as structural Verilog: 1 circuit, main circuit main
module main (
  input  A,
  input  B,
  input  C,
  input  D,
  input  B_2,
  input  D_2,
  output out_7,
  output out_8
);

  wire nor_1_out, not_1_out, xnor_1_out, xor_1_out;

  not not_1 (not_1_out, D);
  nor nor_1 (nor_1_out, A, B);
  xnor xnor_1 (xnor_1_out, C, not_1_out);
  xor xor_1 (xor_1_out, B_2, D_2);
  xor xor_2 (out_7, nor_1_out, xnor_1_out);
  nand nand_1 (out_8, xnor_1_out, xor_1_out);
endmodule
